# Fritzing sketch esca (saved by Fritzing 0.9.4)

parts:
  U2 = LIPO-110mAh [package=lipo-110]  # not connected
  Part1 = Adafruit FONA 808 Breakout [part_number="Adafruit #2542"]
  ESP32_-_Back1 = ESP32 - CAM
  LED1 = LED - 5mm [color="Red (633nm)" package="5 mm [THT]"]
  U3 = DC 5V TO ± 12V Mini DC converter [package=THT]
  R2 = Resistor [tolerance=±5% resistance=220 package="0805 [SMD]"]
  R3 = Resistor [tolerance=±5% resistance=220 package="0805 [SMD]"]  # not connected
  R4 = Resistor [tolerance=±5% resistance=220 package="0805 [SMD]"]
  R1 = Resistor [tolerance=±5% resistance=220 package="0805 [SMD]"]  # not connected
  U1 = LIPO-110mAh [package=lipo-110]
  SW-1 = Vibration sensor module

nets:
  N1: Part1.Bat, Part1.GND, ESP32_-_Back1.GND#12
  N2: Part1.Reset, Part1.RXD, ESP32_-_Back1.GPIO3_/_RX
  N3: Part1.TXD, ESP32_-_Back1.GPIO1_/_TX
  N4: ESP32_-_Back1.GPIO2, SW-1.Digital_output
  N5: ESP32_-_Back1.5V, U3.-12V
  N6: ESP32_-_Back1.3.3V_/_5V_/_P_OUT, SW-1.vcc
  N7: ESP32_-_Back1.GND#16, SW-1.Ground
  N8: LED1.cathode, U3.GND
  N9: R2.Pin_0, U1.+
  N10: R4.Pin_0, U1.-

custom parts:
  Adafruit FONA 808 Breakout: Cellular + GPS tracking, all in one? Oh yes! Introducing Adafruit FONA 808 MiniGSM + GPS, an all-in-one cellular phone module with that lets you add location-tracking, voice, text, SMS and data to your project in an adorable little package.
  ESP32 - CAM: The ESP32-CAM has a very competitive small-size camera module that can operate independently as a minimum system with a footprint of only 27*40.5*4.5mm and a deep sleep current of up to 6mA.
  DC 5V TO ± 12V Mini DC converter: DC 5V TO ± 12V Mini DC converter from ebay (search for "DC 5V TO ± 12V Mini DC converter"). Supplies ± 12V at up to 30MA output for op amps or rs232 drivers from a 3 to 5V input (so a battery or 3.3 or 5V power rail) on a micro).
  Vibration sensor module: Single-roller type full induction trigger switch. When no vibration or tilt, the product is ON conduction state, and in the steady state, when a vibration or tilt, the switch will be rendered instantly disconnect the conductive resistance increases, generating a current pulse signal, thereby triggering circuit. The default state of the swith is close Digital output Supply voltage:3.3V-5V On-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
