# Fritzing sketch esp32cam (saved by Fritzing 0.9.4)

parts:
  U2 = LIPO-110mAh [package=lipo-110]  # not connected
  Part1 = Adafruit FONA 808 Breakout [part_number="Adafruit #2542"]
  ESP32_-_Back1 = ESP32 - CAM
  LED1 = LED - 5mm [color="Red (633nm)" package="5 mm [THT]"]
  U3 = DC 5V TO ± 12V Mini DC converter [package=THT]
  R2 = Resistor [tolerance=±5% resistance=220 package="0805 [SMD]"]
  R3 = Resistor [tolerance=±5% resistance=220 package="0805 [SMD]"]  # not connected
  R4 = Resistor [tolerance=±5% resistance=220 package="0805 [SMD]"]
  R1 = Resistor [tolerance=±5% resistance=220 package="0805 [SMD]"]  # not connected
  U1 = LIPO-110mAh [package=lipo-110]

nets:
  GND: Part1.Bat, Part1.GND, ESP32_-_Back1.GND
  N1: Part1.RXD, ESP32_-_Back1.GPIO3_/_RX
  N2: Part1.TXD, ESP32_-_Back1.GPIO1_/_TX
  N3: ESP32_-_Back1.5V, U3.-12V
  N4: LED1.cathode, U3.GND
  N5: R2.Pin_0, U1.+
  N6: R4.Pin_0, U1.-

custom parts:
  Adafruit FONA 808 Breakout: Cellular + GPS tracking, all in one? Oh yes! Introducing Adafruit FONA 808 MiniGSM + GPS, an all-in-one cellular phone module with that lets you add location-tracking, voice, text, SMS and data to your project in an adorable little package.
  ESP32 - CAM: The ESP32-CAM has a very competitive small-size camera module that can operate independently as a minimum system with a footprint of only 27*40.5*4.5mm and a deep sleep current of up to 6mA.
  DC 5V TO ± 12V Mini DC converter: DC 5V TO ± 12V Mini DC converter from ebay (search for "DC 5V TO ± 12V Mini DC converter"). Supplies ± 12V at up to 30MA output for op amps or rs232 drivers from a 3 to 5V input (so a battery or 3.3 or 5V power rail) on a micro).
