# Fritzing sketch schematic production (saved by Fritzing 0.9.4)
perfboards: 1

parts:
  U5 = SWITCH_SPDT [package=kps-1290]
  GY-NEO6MV4 = SUP500F [package=sup500f]
  GSM_SIM_GPSR_SMS_SIM900_SIM2 = SIM800L [package=THT]
  ESP32_-_Back2 = ESP32 - CAM
  TP2 = TP4056 [chip_label=TP4056 package="DIP (Dual Inline) [THT]"]
  Part2 = DC-DC Power Module (5v)
  BAT2 = Battery Holders [package=lipo-1100mAh]
  R4 = Resistor [tolerance=±5% resistance=1k package="0603 [SMD]"]
  R5 = Resistor [tolerance=±5% resistance=1k package="0603 [SMD]"]
  R6 = Resistor [tolerance=±5% resistance=1k package="0603 [SMD]"]
  SW-2 = Vibration sensor module
  LED2 = smd LED [color="Red (633nm)" package="1206 [SMD]"]

nets:
  N1: U5.O, Part2.Vout
  5V: U5.S, GSM_SIM_GPSR_SMS_SIM900_SIM2.5V, ESP32_-_Back2.5V
  N2: GY-NEO6MV4.RX-I, ESP32_-_Back2.GPIO14
  N3: GY-NEO6MV4.TX-O, ESP32_-_Back2.GPIO15
  N4: GY-NEO6MV4.GND, ESP32_-_Back2.GND#16, SW-2.Ground
  VCC: GY-NEO6MV4.VCC, ESP32_-_Back2.3.3V_/_5V_/_P_OUT, SW-2.vcc
  N5: GSM_SIM_GPSR_SMS_SIM900_SIM2.GND, ESP32_-_Back2.GND#7, Part2.GND*
  N6: GSM_SIM_GPSR_SMS_SIM900_SIM2.SIM_RXD, ESP32_-_Back2.GPIO1_/_TX
  N7: ESP32_-_Back2.GPIO13, LED2.anode
  N8: ESP32_-_Back2.GPIO12, R5.Pin_1, R6.Pin_1
  N9: ESP32_-_Back2.GPIO16, SW-2.Digital_output
  N10: TP2.pin4, Part2.Vin, BAT2.+, R6.Pin_0
  N11: TP2.pin5, Part2.GND, BAT2.-, R5.Pin_0
  N12: R4.Pin_1, LED2.cathode

custom parts:
  ESP32 - CAM: The ESP32-CAM has a very competitive small-size camera module that can operate independently as a minimum system with a footprint of only 27*40.5*4.5mm and a deep sleep current of up to 6mA.
  TP4056: A DIP stand-in part for whatever IC you want. With 6 pins on a 300mil dual inline package (DIP) footprint.
  DC-DC Power Module (5v): DC-DC Power Module based con AMS1117-5.0 Input: DC 6~12V (input power must higher 1V than output power); Output: 5V (+/-0.05V error), 800mA
  Vibration sensor module: Single-roller type full induction trigger switch. When no vibration or tilt, the product is ON conduction state, and in the steady state, when a vibration or tilt, the switch will be rendered instantly disconnect the conductive resistance increases, generating a current pulse signal, thereby triggering circuit. The default state of the swith is close Digital output Supply voltage:3.3V-5V On-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
